// Logisim project tipoR_tipoI.circ as structural Verilog: 1 circuit, main circuit main
module main (
  input  [3:0] ALU_OP
);

  wire ALU_SRC, and_1_out, and_2_out, CLK, REG_W, registerfile_1_p7;
  wire [4:0] multiplexer_1_out;
  wire [5:0] FUNCT, OPCODE;
  wire [25:6] mipsprogramrom_1_p2;
  wire [31:0] adder_1_out, bit_extender_1_out, mips_alu_1_p2, mips_alu_1_p4, mips_ram_1_p7, register_1_q,
       registerfile_1_p1, registerfile_1_p8;

  Adder #(.width(32)) adder_1 (.a(register_1_q), .b(32'h4), .out(adder_1_out));  // open: cin, cout
  Register #(.width(32)) register_1 (.D(adder_1_out), .Q(register_1_q), .clk(CLK));  // open: en, clr
  and and_1 (and_1_out, ~OPCODE[0], ~OPCODE[1], ~OPCODE[2], ~OPCODE[3], ~OPCODE[4], ~OPCODE[5]);  // AND_Gate
  and and_2 (and_2_out, FUNCT[0], ~FUNCT[1], ~FUNCT[2], ~FUNCT[3], ~FUNCT[4], FUNCT[5]);  // AND_Gate
  and and_3 (REG_W, and_1_out, and_2_out);
  // MIPSProgramROM mipsprogramrom_1: pin names not known; wires that end beside it: register_1_q, {OPCODE, mipsprogramrom_1_p2, FUNCT}
  Clock CLOCK (.out(CLK));
  not not_1 (ALU_SRC, REG_W);
  Multiplexer #(.width(5), .enable("false")) multiplexer_1 (
    .in0(mipsprogramrom_1_p2[15:11]), .in1(mipsprogramrom_1_p2[20:16]), .out(multiplexer_1_out), .sel(ALU_SRC));
  // RegisterFile registerfile_1: pin names not known; wires that end beside it: registerfile_1_p1, CLK, REG_W, multiplexer_1_out, mipsprogramrom_1_p2[25:21], mipsprogramrom_1_p2[20:16], registerfile_1_p7, registerfile_1_p8
  assign bit_extender_1_out = {{16{1'b0}}, {mipsprogramrom_1_p2[15:6], FUNCT}};  // Bit_Extender bit_extender_1
  // Mips_ALU mips_alu_1: pin names not known; wires that end beside it: registerfile_1_p7, mips_alu_1_p2, ALU_OP, mips_alu_1_p4
  Multiplexer #(.width(32), .enable("false")) multiplexer_2 (
    .in0(registerfile_1_p8), .in1(bit_extender_1_out), .out(mips_alu_1_p2), .sel(ALU_SRC));
  // MIPS_RAM mips_ram_1: pin names not known; wires that end beside it: mips_alu_1_p4[19:0], registerfile_1_p8, ALU_SRC, CLK, ALU_SRC, ALU_SRC, mips_ram_1_p7
  Multiplexer #(.width(32), .enable("false")) multiplexer_3 (
    .in0(mips_alu_1_p4), .in1(mips_ram_1_p7), .out(registerfile_1_p1), .sel(ALU_SRC));

  // Other names for the same wires on the sheet: LOAD = ALU_SRC; MEM_TO_REG = ALU_SRC; REG_DEST = ALU_SRC;
  //   RESET = ALU_SRC; STORE = ALU_SRC

  // Notes on the sheet:
  //   tipo R
  //   tipo I
  //   DADO
  //   (controle)
  //   END
  //   END
  //   END
  //   DESTINO
  //   ORIGEM 2
  //   ORIGEM 1
  //   DADO
  //   tipo R
  //   tipo I
  //   SOMA
endmodule
